# Fritzing sketch UltrasonicStriker (saved by Fritzing 0.9.3b)

parts:
  Part1 = Adafruit 16-Channel PWM + Servo HAT [part_number="Adafruit #2327"]
  S1 = H-Bridge with L298N
  L1 = Solenoid [part_number="Universal Power Door Lock Actuator"]
  Part2 = DC-DC Power Module (3.3v) [part_number="XL6009 Step-up Power Module"]
  MOTOR1 = 28BYJ-48 Stepper Motor
  X1 = X113647 Stepper Driver Board [package=board]
  J1 = Basic Servo
  VCC1 = 4 x AAA Battery Mount [part_number="4.8v Usb power module"]  # not connected
  hc-sr1 = hc-sr04
  X2 = X113647 Stepper Driver Board [package=board]
  R1 = Resistor [tolerance=±5% resistance=680 package="0603 [SMD]"]
  R2 = Resistor [tolerance=±5% resistance=1k package="0603 [SMD]"]
  MOTOR2 = 28BYJ-48 Stepper Motor

nets:
  N1: Part1.PWRIN, S1.5V
  GND: Part1.GND, S1.GND, Part2.GND*, X1.GND, J1.gnd, hc-sr1.GND, X2.GND, R2.Pin_1
  N2: Part1.GPIO4, X2.IN1
  N3: Part1.GPIO17, X2.IN2
  N4: Part1.GPIO18, X2.IN3
  N5: Part1.GPIO27, X2.IN4
  N6: Part1.GPIO22, S1.IN1
  N7: Part1.GPIO23, S1.IN2
  N8: Part1.GPIO12, X1.IN1
  N9: Part1.GPIO13, X1.IN2
  N10: Part1.GPIO16, X1.IN3
  N11: Part1.GPIO19, X1.IN4
  N12: Part1.GPIO20, Part1.N$4, R1.Pin_1, R2.Pin_0
  N13: Part1.GPIO21, hc-sr1.Trig
  N14: Part1.#4, J1.pulse
  +5V: Part1.+5V, X1.+V, J1.vcc, X2.+V
  N15: Part1.5.0V, hc-sr1.VCC
  N16: Part1.N$23, hc-sr1.Echo
  N17: Part1.N$42, R1.Pin_0
  N18: S1.12V, Part2.Vout
  N19: S1.M1-01, L1.pin2
  N20: S1.M1-02, L1.pin1
  N21: MOTOR1.BLUE, X1.BLUE
  N22: X2.RED, MOTOR2.BLUE

notes:
  Triange striker attached to end of servo (not shown)
  Simple Voltage Divider for ultrasonic sensor
  Using pins 14 and 15 for 5 volt power

custom parts:
  Adafruit 16-Channel PWM + Servo HAT: The Raspberry Pi is a wonderful little computer, but one thing it isn't very good at is controlling DC Servo Motors - these motors need very specific and repetitive timing pulses to set the position. Instead of asking the Pi Linux kernel to send these signals, pop on this handy HAT! It adds the capability to control 16 Servos with perfect timing. It can also do PWM up to 1.6 KHz with 12 bit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
  H-Bridge with L298N: h-bridge
  DC-DC Power Module (3.3v): DC-DC Power Module based con AMS1117-3.3 Input: DC 4.5~7V (input power must higher 1V than output power); Output: 3.3V (+/-0.05V error), 800mA
  28BYJ-48 Stepper Motor: 28BYJ-48 gear-reduction stepper motor (small)
  X113647 Stepper Driver Board: A common stepper motor driver board based on ULN2003APG darlington array

// code stored in the sketch: Untitled3.ino
import RPi.GPIO as GPIO
from time import sleep

GPIO.setmode(GPIO.BOARD)
GPIO.setup(13, GPIO.OUT)
GPIO.setup(15, GPIO.OUT)

def forward(x):
    GPIO.output(13, GPIO.HIGH)
    sleep(x)
    GPIO.output(13, GPIO.LOW)

def reverse(x):
    GPIO.output(15, GPIO.HIGH)
    sleep(x)
    GPIO.output(15, GPIO.LOW)

forward(3)
sleep(0.5)
reverse(3)

GPIO.cleanup()
